# Fritzing sketch LFSR_hardware (saved by Fritzing 1.0.7)
breadboards: 1

parts:
  U1 = 74HC595 [package="DIP16 [THT]"]
  Part1 = Arduino Uno (Rev3)
  LED0 = LED - 3mm [color="Red (633nm)" current=0.030A package="3 mm [THT]"]
  LED1 = LED - 3mm [color="Red (633nm)" current=0.030A package="3 mm [THT]"]
  LED3 = LED - 3mm [color="Red (633nm)" current=0.030A package="3 mm [THT]"]
  LED4 = LED - 3mm [color="Red (633nm)" current=0.030A package="3 mm [THT]"]
  LED5 = LED - 3mm [color="Red (633nm)" current=0.030A package="3 mm [THT]"]
  LED6 = LED - 3mm [color="Red (633nm)" current=0.030A package="3 mm [THT]"]
  LED7 = LED - 3mm [color="Red (633nm)" current=0.030A package="3 mm [THT]"]
  P1 = Rotary Potentiometer (Small) [maximum_resistance=10kΩ knob_status=50% power=0.5W package=THT]
  S2 = Pushbutton [package="[THT]"]
  S3 = Pushbutton [package="[THT]"]
  U3 = 4070 4 x 2 Input XOR Gate, single part [part_number=4070 package="DIP (Dual Inline) [THT]"]
  R0 = Resistor [tolerance=±5% power=0.25W resistance=220 package=THT]
  R1 = Resistor [tolerance=±5% power=0.25W resistance=220 package=THT]
  R2 = Resistor [tolerance=±5% power=0.25W resistance=220 package=THT]
  R3 = Resistor [tolerance=±5% power=0.25W resistance=220 package=THT]
  R4 = Resistor [tolerance=±5% power=0.25W resistance=220 package=THT]
  R5 = Resistor [tolerance=±5% power=0.25W resistance=220 package=THT]
  R6 = Resistor [tolerance=±5% power=0.25W resistance=220 package=THT]
  R7 = Resistor [tolerance=±5% power=0.25W resistance=220 package=THT]
  LED2 = LED - 3mm [color="Red (633nm)" current=0.030A package="3 mm [THT]"]
  S1 = Toggle Switch [package=THT]

nets:
  N1: U1.Q1, U3.A4, R6.Pin_0
  N2: U1.Q2, U3.B3, R5.Pin_0
  N3: U1.Q3, R4.Pin_0
  N4: U1.Q4, R3.Pin_0
  N5: U1.Q5, U3.A2, R2.Pin_0
  N6: U1.Q6, R1.Pin_0
  N7: U1.Q7, U3.B1, R0.Pin_0
  GND: U1.GND, U1.OE, Part1.GND, LED0.cathode, LED1.cathode, LED3.cathode, LED4.cathode, LED5.cathode, LED6.cathode, LED7.cathode, P1.leg2, S2.Pin_1, S2.Pin_2, S3.Pin_1, S3.Pin_2, U3.GND, LED2.cathode, S1.COM
  N8: U1.MR, Part1.D7
  N9: U1.SH_CP, Part1.D9_PWM
  N10: U1.ST_CP, Part1.D11_PWM/MOSI
  N11: U1.DS, U3.Q3
  N12: U1.Q0, R7.Pin_0
  VCC: U1.VCC, Part1.5V, P1.leg1, U3.VDD
  N13: Part1.A0, P1.wiper
  N14: Part1.D12/MISO, U3.A1
  N15: Part1.D2, S3.Pin_3, S3.Pin_4
  N16: Part1.D3_PWM, S2.Pin_3, S2.Pin_4
  N17: Part1.D4, S1.L1
  N18: LED0.anode, R0.Pin_1
  N19: LED1.anode, R1.Pin_1
  N20: LED3.anode, R3.Pin_1
  N21: LED4.anode, R4.Pin_1
  N22: LED5.anode, R5.Pin_1
  N23: LED6.anode, R6.Pin_1
  N24: LED7.anode, R7.Pin_1
  N25: U3.Q1, U3.B2
  N26: U3.Q2, U3.B4
  N27: U3.A3, U3.Q4
  N28: R2.Pin_1, LED2.anode

notes:
  SET
  STEP
  A/M
  7 | 6 | 5 | 4 | 3 | 2 | 1 | 0
  SPEED
